# Fritzing sketch EmbeddedCarSchematics (saved by Fritzing 0.9.3b)
breadboards: 1

parts:
  Part1 = Arduino Mega 2560 (Rev3)
  Part2 = Thumb Joystick
  HC-SR04_Sensor_1 = HC-SR04 Ultrasonic Distance Sensor
  RHT1 = Humidity and Temperature Sensor RHT03
  U1 = SM130 [package=sm130]
  IC1 = DS1307 [package=THT]
  Part3 = Bluetooth HC-05 Macho
  R1 = Photocell (LDR) [package=THT]
  U4 = LCD_CFAX [package=lcd_cfax]
  S1 = Round Pushbutton
  Part4 = Arduino Motor Shield
  SG1 = Buzzer 12mm [package=buzzer-ccv-kit]
  BAT1 = BC9VPC [package=bc9vpc]
  BAT2 = BC9VPC [package=bc9vpc]
  M2 = DC Motor  # not connected
  M3 = DC Motor  # not connected
  M4 = DC Motor  # not connected
  M1 = DC Motor  # not connected
  LED1 = LED - 5mm [color="Yellow (595nm)" package="5 mm [THT]"]
  LED2 = LED - 5mm [color="Yellow (595nm)" package="5 mm [THT]"]

nets:
  N1: Part1.A0, U4.D5
  N2: Part1.A1, U4.D6
  N3: Part1.A2, U4.D7
  N4: Part1.A3, U4.MI
  N5: Part1.A4, U4.P_S
  N6: Part1.A5, R1.pin_1
  N7: Part1.A6, Part2.HORZ
  N8: Part1.A7, Part2.VERT
  N9: Part1.D21/SCL, IC1.SCL_-_I2C_Clock
  N10: Part1.D20/SDA, IC1.SWQ/OUT_-_Clock_Output
  N11: Part1.D19/RX1, Part3.RXD
  N12: Part1.D18/TX1, Part3.TXD
  N13: Part1.D12_PWM, S1.leg1
  N14: Part1.D11_PWM, Part4.3.3V
  N15: Part1.D10_PWM, Part4.RES
  N16: Part1.D9_PWM, U4.D1
  N17: Part1.D8_PWM, U4.D0
  N18: Part1.3V3, U1.RFVCC
  VCC: Part1.5V, Part2.VCC, HC-SR04_Sensor_1.VCC, RHT1.Vcc, IC1.+V, Part3.VCC, U4.D3
  GND: Part1.GND, Part2.GND, HC-SR04_Sensor_1.GND, RHT1.GND_2, U1.GND, IC1.0V, Part3.GND, R1.pin_0, U4.D4, S1.leg0, Part4.GND, SG1.2, BAT1.V-, LED1.cathode
  N19: Part1.D1_TX0, U4.GND
  N20: Part1.D2_PWM, U4.CS1B
  N21: Part1.D3_PWM, U4.CS2
  N22: Part1.D4_PWM, U4.RESET
  N23: Part1.D5_PWM, U4.RS
  N24: Part1.D6_PWM, U4.RW
  N25: Part1.D7_PWM, U4.ERD
  N26: Part1.D30, Part4.OUT3
  N27: Part1.D31, Part4.OUT1
  N28: Part1.D32, Part4.OUT4
  N29: Part1.D33, Part4.OUT2
  N30: Part1.D35, HC-SR04_Sensor_1.TRIG
  N31: Part1.D37, HC-SR04_Sensor_1.ECHO
  N32: Part1.D40, LED1.anode
  N33: Part1.D41, LED2.anode
  N34: Part1.D42, RHT1.Data-signal, SG1.1
  N35: Part1.D49, U1.ANT1
  N36: Part1.D50, U1.RFGND
  N37: Part1.D51, U1.O2
  N38: Part1.D52, U1.O1
  N39: Part1.D53, U1.I2
  N40: Part4.VIN, BAT1.V+, BAT2.V+
